# Fritzing sketch WattThrustMeter (saved by Fritzing 0.9.6b)
breadboards: 1

parts:
  Part1 = Arduino Nano (Rev3.0)
  S2_-_Test = Momentary Switch [package=ksa_sealed_tac_switch]
  S4_-_OK = Momentary Switch [package=ksa_sealed_tac_switch]
  R1 = Rotary Potentiometer (Small) [maximum_resistance=10kΩ package=THT]
  S3_-_Previous = Momentary Switch [package=ksa_sealed_tac_switch]
  R2 = Resistor [tolerance=±5% resistance=47k power=0.25 package=THT]
  Part2 = ACS712 Low Current Sensor Board v12
  S5_-_THRCUT = Momentary Switch [package=ksa_sealed_tac_switch]
  Part3 = HX711 Weighing Sensor Module
  J1 = Basic Servo
  S1_-_Page = Momentary Switch [package=ksa_sealed_tac_switch]
  R3 = Resistor [tolerance=±20% power=0.25 resistance=10k package=THT]

nets:
  GND: Part1.GND, R1.leg1, Part2.GND, Part3.GND, J1.gnd, R3.Pin_0
  N1: Part1.D3, S2_-_Test.2, S4_-_OK.2, S3_-_Previous.2, S5_-_THRCUT.2, S1_-_Page.2
  N2: Part1.D4, S1_-_Page.4
  N3: Part1.D5, S4_-_OK.4
  N4: Part1.D6, S3_-_Previous.4
  N5: Part1.D7, S2_-_Test.4
  N6: Part1.D8, S5_-_THRCUT.4
  N7: Part1.D9, Part3.DO/RX
  N8: Part1.D10, Part3.CK/TX
  N9: Part1.D11/MOSI, J1.pulse
  5V: Part1.VIN
  5V_2: Part1.5V, R1.leg2, Part2.5V, Part3.VCC, J1.vcc
  N10: Part1.A7, R1.wiper
  LCD SCL: Part1.A5
  LCD SDA: Part1.A4
  N11: Part1.A3, R2.Pin_1, R3.Pin_1
  N12: Part1.A1, Part2.VO
  Vbat: R2.Pin_0
